# Fritzing sketch user-controlled-led-color (saved by Fritzing 0.9.3b)
breadboards: 1

parts:
  Teensy_3_1 = Teensy 3.1  # not connected
  LED1 = RGB LED (com. cathode, rgb) [package="5 mm [THT]"]
  R1 = Resistor [tolerance=±5% resistance=220 package="2512 [SMD]"]
  S1 = Pushbutton [package="[THT]"]
  S2 = Pushbutton [package="[THT]"]
  R2 = Resistor [tolerance=±5% resistance=220 package="2512 [SMD]"]
  R3 = Resistor [tolerance=±5% resistance=220 package="2512 [SMD]"]
  R4 = Resistor [tolerance=±5% resistance=10k package="2512 [SMD]"]
  R5 = Trimmer Potentiometer [maximum_resistance=10kΩ package=THT]

nets:
  N1: LED1.red_anode, R1.Pin_1
  N2: LED1.common_cathode, S1.Pin_1, S1.Pin_2, S2.Pin_1, S2.Pin_2, R5.leg1
  N3: LED1.green_anode, R2.Pin_1
  N4: LED1.blue_anode, R3.Pin_1
  N5: S1.Pin_3, S1.Pin_4, R4.Pin_1
  N6: S2.Pin_3, S2.Pin_4
  N7: R4.Pin_0, R5.leg2

notes:
  CST8227 – Interfacing
  Lab 06 – User Controlled LED Color
  Use a potentiometer as user input to control the LED color.
  @author Lucas Estienne (esti0011)
